// Logisim project 4bit adder.circ as structural Verilog: 2 circuits, main circuit main
module main (
  input  A,
  input  B,
  input  C,
  input  D,
  output Sum,
  output Carry
);

  _4_bit_Adder u_4_bit_adder_1 (.D(A), .C(B), .B(C), .A(D), .Sum(Sum), .Carry(Carry));
endmodule

module _4_bit_Adder (
  input  D,
  input  C,
  input  B,
  input  A,
  output Sum,
  output Carry
);

  wire and_2_out, and_3_out, and_4_out, and_5_out, not_1_out, not_2_out, not_3_out, not_4_out, not_5_out,
       not_6_out, not_7_out, not_8_out, not_9_out, not_10_out, not_11_out, not_12_out;

  not not_1 (not_1_out, D);
  not not_2 (not_2_out, C);
  not not_3 (not_3_out, B);
  not not_4 (not_4_out, D);
  not not_5 (not_5_out, C);
  not not_6 (not_6_out, A);
  not not_7 (not_7_out, D);
  not not_8 (not_8_out, B);
  not not_9 (not_9_out, A);
  not not_10 (not_10_out, C);
  not not_11 (not_11_out, B);
  not not_12 (not_12_out, A);
  and and_1 (Carry, D, C, B, A);
  and and_2 (and_2_out, not_1_out, not_2_out, not_3_out, A);
  and and_3 (and_3_out, not_4_out, not_5_out, B, not_6_out);
  and and_4 (and_4_out, not_7_out, C, not_8_out, not_9_out);
  and and_5 (and_5_out, D, not_10_out, not_11_out, not_12_out);
  or or_1 (Sum, and_2_out, and_3_out, and_4_out, and_5_out);
endmodule
