// Logisim project BCD TO 7SEGMENT.circ as structural Verilog: 2 circuits, main circuit main
module main (
  input  in_1,
  input  in_2,
  input  in_3,
  input  in_4
);

  wire test_1_a, test_1_b, test_1_c, test_1_d, test_1_e, test_1_f, test_1_g;

  test test_1 (
    .W(in_1), .X(in_2), .a(test_1_a), .Y(in_3), .Z(in_4), .b(test_1_b), .c(test_1_c), .d(test_1_d),
    .e(test_1_e), .f(test_1_f), .g(test_1_g));
  _7_Segment_Display u_7_segment_display_1 (
    .g(test_1_g), .f(test_1_f), .a(test_1_a), .b(test_1_b), .e(test_1_e), .d(test_1_d), .c(test_1_c));  // open: dp
endmodule

module test (
  input  W,
  input  X,
  input  Y,
  input  Z,
  output a,
  output b,
  output c,
  output d,
  output e,
  output f,
  output g
);

  wire and_1_out, and_2_out, and_3_out, and_4_out, and_5_out, and_6_out, and_7_out, and_8_out, and_9_out,
       and_10_out, and_11_out, and_12_out, and_13_out, and_14_out, and_15_out, and_16_out, and_17_out,
       and_18_out, and_19_out, not_1_out, not_2_out, not_3_out, not_4_out, not_5_out, not_6_out, not_7_out,
       not_8_out, not_9_out, not_10_out, not_11_out, not_12_out, not_13_out, not_14_out, not_15_out,
       not_16_out, not_17_out, not_18_out, not_19_out, not_20_out, not_21_out, not_22_out;

  not not_1 (not_1_out, X);
  and and_1 (and_1_out, not_1_out, not_2_out);
  not not_2 (not_2_out, Z);
  and and_2 (and_2_out, X, Z);
  not not_3 (not_3_out, X);
  not not_4 (not_4_out, Y);
  and and_3 (and_3_out, not_4_out, not_5_out);
  not not_5 (not_5_out, Z);
  and and_4 (and_4_out, Y, Z);
  not not_6 (not_6_out, Y);
  or or_1 (c, not_6_out, Z, X);
  not not_7 (not_7_out, X);
  and and_5 (and_5_out, not_7_out, not_8_out);
  not not_8 (not_8_out, Z);
  not not_9 (not_9_out, X);
  and and_6 (and_6_out, not_9_out, Y);
  and and_7 (and_7_out, Y, not_10_out);
  not not_10 (not_10_out, Z);
  and and_8 (and_8_out, X, not_11_out, Z);
  not not_11 (not_11_out, Y);
  and and_9 (and_9_out, W, not_12_out);
  not not_12 (not_12_out, X);
  not not_13 (not_13_out, X);
  and and_10 (and_10_out, not_13_out, not_14_out);
  not not_14 (not_14_out, Z);
  and and_11 (and_11_out, Y, not_15_out);
  not not_15 (not_15_out, Z);
  and and_12 (and_12_out, W, Y);
  and and_13 (and_13_out, W, X);
  not not_16 (not_16_out, Y);
  and and_14 (and_14_out, not_16_out, not_17_out);
  not not_17 (not_17_out, Z);
  and and_15 (and_15_out, X, not_18_out);
  not not_18 (not_18_out, Y);
  and and_16 (and_16_out, X, not_19_out);
  not not_19 (not_19_out, Z);
  not not_20 (not_20_out, X);
  and and_17 (and_17_out, not_20_out, Y);
  and and_18 (and_18_out, X, not_21_out);
  not not_21 (not_21_out, Y);
  and and_19 (and_19_out, X, not_22_out);
  not not_22 (not_22_out, Z);
  or or_2 (a, and_1_out, Y, and_2_out, W);
  or or_3 (b, not_3_out, and_3_out, and_4_out);
  or or_4 (d, and_5_out, and_6_out, and_7_out, and_8_out, and_9_out);
  or or_5 (e, and_10_out, and_11_out, and_12_out, and_13_out);
  or or_6 (f, and_14_out, and_15_out, and_16_out, W);
  or or_7 (g, and_17_out, and_18_out, and_19_out, W);
endmodule
